# Fritzing sketch central_module (saved by Fritzing 0.9.3b)
breadboards: 1

parts:
  Part1 = Arduino Nano (Rev3.0)
  Part2 = NRF24L01+ Breakout Board
  U1 = Mini-USB _B_ connector with 5th pin broken out. [package=usb-minib]

nets:
  N1: Part1.D1/TX, U1.D-
  N2: Part1.D0/RX, U1.D+
  GND: Part1.GND, Part2.GND, U1.GND
  N3: Part1.D9, Part2.CE
  N4: Part1.D10, Part2.CS
  N5: Part1.D11/MOSI, Part2.MOSI
  N6: Part1.D12/MISO, Part2.MISO
  N7: Part1.5V, U1.VBUS
  3V3: Part1.3V3, Part2.VCC
  N8: Part1.D13/SCK, Part2.SCK
