# Fritzing sketch train_module (saved by Fritzing 0.9.3b)
breadboards: 1

parts:
  Part2 = Arduino Nano (Rev3.0) (ICSP)
  VCC1 = Battery
  M1 = DC Motor
  D1 = Rectifier Diode [part_number=1N4004 package="300 mil [THT]"]
  T1 = TRANSISTOR_NPN_2 [part_number=2n2222 package=to-92]
  R1 = Resistor [tolerance=±5% resistance=1k package="0805 [SMD]"]
  VCC2 = Battery block 9V
  Part1 = NRF24L01+ Breakout Board
  LED1 = LEDs [package=led10mm]
  LED2 = LEDs [package=led10mm]
  R2 = Resistor [tolerance=±5% resistance=220 package="0805 [SMD]"]
  R3 = Resistor [tolerance=±5% resistance=220 package="0805 [SMD]"]

nets:
  GND: Part2.GND, VCC1.-, T1.E, VCC2.-, Part1.GND, LED1.C, LED2.C
  N1: Part2.D6, R1.Pin_1
  N2: Part2.D7, R3.Pin_0
  N3: Part2.D8, R2.Pin_0
  N4: Part2.D9, Part1.CE
  N5: Part2.D10, Part1.CS
  N6: Part2.VIN, VCC2.+
  3V3: Part2.3V3, Part1.VCC
  N7: Part2.D12/MISO, Part1.MISO
  N8: Part2.D13/SCK, Part1.SCK
  N9: Part2.D11/MOSI, Part1.MOSI
  N10: VCC1.+, M1.pin_1, D1.cathode
  N11: M1.pin_2, D1.anode, T1.C
  N12: T1.B, R1.Pin_0
  N13: LED1.A, R2.Pin_1
  N14: LED2.A, R3.Pin_1
