# Fritzing sketch vacancy_module (saved by Fritzing 0.9.3b)
breadboards: 1

parts:
  R1 = PHOTOCELL [package=photocell]
  Part1 = Arduino Nano (Rev3.0)
  R2 = PHOTOCELL [package=photocell]
  R3 = PHOTOCELL [package=photocell]
  R4 = PHOTOCELL [package=photocell]
  R5 = PHOTOCELL [package=photocell]
  R6 = PHOTOCELL [package=photocell]
  R7 = PHOTOCELL [package=photocell]
  R8 = PHOTOCELL [package=photocell]
  R9 = Resistor [tolerance=±5% resistance=220 package="1206 [SMD]"]
  R10 = Resistor [tolerance=±5% resistance=220 package="1206 [SMD]"]
  R11 = Resistor [tolerance=±5% resistance=220 package="1206 [SMD]"]
  R12 = Resistor [tolerance=±5% resistance=220 package="1206 [SMD]"]
  R13 = Resistor [tolerance=±5% resistance=220 package="1206 [SMD]"]
  R14 = Resistor [tolerance=±5% resistance=220 package="1206 [SMD]"]
  R15 = Resistor [tolerance=±5% resistance=220 package="1206 [SMD]"]
  R16 = Resistor [tolerance=±5% resistance=220 package="1206 [SMD]"]
  LED1 = LED - 3mm [color="Red (633nm)" package="3 mm [THT]"]
  R17 = Resistor [tolerance=±5% resistance=220 package="1206 [SMD]"]
  LED2 = LED - 3mm [color="Red (633nm)" package="3 mm [THT]"]
  R18 = Resistor [tolerance=±5% resistance=220 package="1206 [SMD]"]
  LED3 = LED - 3mm [color="Red (633nm)" package="3 mm [THT]"]
  R19 = Resistor [tolerance=±5% resistance=220 package="1206 [SMD]"]
  LED4 = LED - 3mm [color="Red (633nm)" package="3 mm [THT]"]
  R20 = Resistor [tolerance=±5% resistance=220 package="1206 [SMD]"]
  LED5 = LED - 3mm [color="Red (633nm)" package="3 mm [THT]"]
  R21 = Resistor [tolerance=±5% resistance=220 package="1206 [SMD]"]
  LED6 = LED - 3mm [color="Red (633nm)" package="3 mm [THT]"]
  R22 = Resistor [tolerance=±5% resistance=220 package="1206 [SMD]"]
  LED7 = LED - 3mm [color="Red (633nm)" package="3 mm [THT]"]
  R23 = Resistor [tolerance=±5% resistance=220 package="1206 [SMD]"]
  LED8 = LED - 3mm [color="Red (633nm)" package="3 mm [THT]"]
  R24 = Resistor [tolerance=±5% resistance=220 package="1206 [SMD]"]
  BAT1 = BC9VPC [package=bc9vpc]
  Part2 = NRF24L01+ Breakout Board

nets:
  N1: R1.P$1, Part1.5V, R2.P$1, R3.P$1, R4.P$1, R5.P$1, R6.P$1, R7.P$1, R8.P$1
  N2: R1.P$2, Part1.A0, R9.Pin_1
  N3: Part1.D1/TX, R24.Pin_1
  GND: Part1.GND, R9.Pin_0, R10.Pin_0, R11.Pin_0, R12.Pin_0, R13.Pin_0, R14.Pin_0, R15.Pin_0, R16.Pin_0, LED1.cathode, LED2.cathode, LED3.cathode, LED4.cathode, LED5.cathode, LED6.cathode, LED7.cathode, LED8.cathode, BAT1.V-, Part2.GND
  N4: Part1.D2, R23.Pin_1
  N5: Part1.D3, R22.Pin_1
  N6: Part1.D4, R21.Pin_1
  N7: Part1.D5, R20.Pin_1
  N8: Part1.D6, R19.Pin_1
  N9: Part1.D7, R18.Pin_1
  N10: Part1.D8, R17.Pin_1
  N11: Part1.D9, Part2.CE
  N12: Part1.D10, Part2.CS
  N13: Part1.D11/MOSI, Part2.MOSI
  N14: Part1.D12/MISO, Part2.MISO
  N15: Part1.VIN, BAT1.V+
  N16: Part1.A7, R8.P$2, R16.Pin_1
  N17: Part1.A6, R7.P$2, R15.Pin_1
  N18: Part1.A5, R6.P$2, R14.Pin_1
  N19: Part1.A4, R5.P$2, R13.Pin_1
  N20: Part1.A3, R4.P$2, R12.Pin_1
  N21: Part1.A2, R3.P$2, R11.Pin_1
  N22: Part1.A1, R2.P$2, R10.Pin_1
  3V3: Part1.3V3, Part2.VCC
  N23: Part1.D13/SCK, Part2.SCK
  N24: LED1.anode, R17.Pin_0
  N25: LED2.anode, R18.Pin_0
  N26: LED3.anode, R19.Pin_0
  N27: LED4.anode, R20.Pin_0
  N28: LED5.anode, R21.Pin_0
  N29: LED6.anode, R22.Pin_0
  N30: LED7.anode, R23.Pin_0
  N31: LED8.anode, R24.Pin_0
